// Logisim project GRO circuit file.circ as structural Verilog: 1 circuit, main circuit main
module main (
  input  [11:0] in_1,
  input  in_2,
  input  [3:0] in_3,
  input  [3:0] in_4,
  input  in_5,
  input  [3:0] in_6,
  output out_7,
  output [3:0] out_8,
  output [2:0] out_9,
  output [2:0] out_10,
  output [2:0] out_11,
  output [2:0] out_12
);

  wire clock_1_out;
  wire [3:0] adder_1_out, adder_2_out, adder_3_out, adder_4_out, demultiplexer_1_out0, demultiplexer_1_out1,
       demultiplexer_1_out2, demultiplexer_1_out3, demultiplexer_1_out4, demultiplexer_1_out5,
       demultiplexer_1_out6, demultiplexer_1_out7, multiplexer_1_out, multiplexer_2_out, not_1_out, or_1_out,
       register_1_q, register_2_q, register_3_q, register_4_q, register_5_q, register_6_q, register_7_q,
       register_8_q, subtractor_1_out, xor_1_out;

  Demultiplexer #(.select(3), .width(4), .enable("false")) demultiplexer_1 (
    .out0(demultiplexer_1_out0), .out1(demultiplexer_1_out1), .out2(demultiplexer_1_out2),
    .out3(demultiplexer_1_out3), .out4(demultiplexer_1_out4), .out5(demultiplexer_1_out5),
    .out6(demultiplexer_1_out6), .out7(demultiplexer_1_out7), .in(out_8), .sel(in_1[5:3]));
  Register #(.width(4)) register_1 (
    .D(demultiplexer_1_out0), .en(in_2), .Q(register_1_q), .clk(clock_1_out));  // open: clr
  Register #(.width(4)) register_2 (
    .D(demultiplexer_1_out1), .en(in_2), .Q(register_2_q), .clk(clock_1_out));  // open: clr
  Register #(.width(4)) register_3 (
    .D(demultiplexer_1_out2), .en(in_2), .Q(register_3_q), .clk(clock_1_out));  // open: clr
  Register #(.width(4)) register_4 (
    .D(demultiplexer_1_out3), .en(in_2), .Q(register_4_q), .clk(clock_1_out));  // open: clr
  Register #(.width(4)) register_5 (
    .D(demultiplexer_1_out4), .en(in_2), .Q(register_5_q), .clk(clock_1_out));  // open: clr
  Register #(.width(4)) register_6 (
    .D(demultiplexer_1_out5), .en(in_2), .Q(register_6_q), .clk(clock_1_out));  // open: clr
  Register #(.width(4)) register_7 (
    .D(demultiplexer_1_out6), .en(in_2), .Q(register_7_q), .clk(clock_1_out));  // open: clr
  Register #(.width(4)) register_8 (
    .D(demultiplexer_1_out7), .en(in_2), .Q(register_8_q), .clk(clock_1_out));  // open: clr
  Clock clock_1 (.out(clock_1_out));
  Multiplexer #(.select(3), .width(4), .enable("false")) multiplexer_1 (
    .in0(register_1_q), .in1(register_2_q), .in2(register_3_q), .in3(register_4_q), .in4(register_5_q),
    .in5(register_6_q), .in6(register_7_q), .in7(register_8_q), .out(multiplexer_1_out), .sel(in_1[11:9]));
  Multiplexer #(.select(3), .width(4), .enable("false")) multiplexer_2 (
    .in0(register_1_q), .in1(register_2_q), .in2(register_3_q), .in3(register_4_q), .in4(register_5_q),
    .in5(register_6_q), .in6(register_7_q), .in7(register_8_q), .out(multiplexer_2_out), .sel(in_1[8:6]));
  assign or_1_out = multiplexer_2_out | multiplexer_1_out;  // OR_Gate or_1, 4 bits wide
  Adder #(.width(4)) adder_1 (.a(multiplexer_1_out), .b(in_3), .out(adder_1_out));  // open: cin, cout
  Adder #(.width(4)) adder_2 (.a(multiplexer_2_out), .b(in_4), .out(adder_2_out));  // open: cin, cout
  Adder #(.width(4)) adder_3 (
    .a(multiplexer_2_out), .b(multiplexer_1_out), .out(adder_3_out), .cout(out_7));  // open: cin
  Subtractor #(.width(4)) subtractor_1 (
    .a(multiplexer_1_out), .b(multiplexer_2_out), .out(subtractor_1_out), .bin(in_5));  // open: bout
  Adder #(.width(4)) adder_4 (.a(multiplexer_1_out), .b(in_6), .out(adder_4_out));  // open: cin, cout
  assign xor_1_out = multiplexer_1_out ^ multiplexer_2_out;  // XOR_Gate xor_1, 4 bits wide
  assign not_1_out = ~multiplexer_1_out;  // NOT_Gate not_1, 4 bits wide
  Multiplexer #(.select(3), .width(4), .enable("false")) multiplexer_3 (
    .in0(or_1_out), .in1(adder_1_out), .in2(adder_2_out), .in3(adder_3_out), .in4(subtractor_1_out),
    .in5(adder_4_out), .in6(xor_1_out), .in7(not_1_out), .out(out_8), .sel(in_1[2:0]));

  assign out_9 = in_1[2:0];
  assign out_10 = in_1[11:9];
  assign out_11 = in_1[8:6];
  assign out_12 = in_1[5:3];
endmodule
